// Logisim project ALU.circ as structural Verilog: 4 circuits, main circuit main
module main (
  input  [7:0] A,
  input  [7:0] B,
  input  [5:0] Opcode,
  output [7:0] out_4
);

  wire adder_1_carry_out, adder_2_carry_out, adder_3_carry_out, adder_4_carry_out, adder_5_carry_out,
       adder_6_carry_out, adder_7_carry_out;

  Adder adder_1 (
    .INVA(Opcode[1]), .A(A[7]), .ENA(Opcode[3]), .B(B[7]), .ENB(Opcode[2]), .Carry_in(Opcode[0]),
    .F0(Opcode[5]), .F1(Opcode[4]), .Carry_out(adder_1_carry_out), .Output(out_4[7]));
  Adder adder_2 (
    .INVA(Opcode[1]), .A(A[6]), .ENA(Opcode[3]), .B(B[6]), .ENB(Opcode[2]), .Carry_in(adder_1_carry_out),
    .F0(Opcode[5]), .F1(Opcode[4]), .Carry_out(adder_2_carry_out), .Output(out_4[6]));
  Adder adder_3 (
    .INVA(Opcode[1]), .A(A[5]), .ENA(Opcode[3]), .B(B[5]), .ENB(Opcode[2]), .Carry_in(adder_2_carry_out),
    .F0(Opcode[5]), .F1(Opcode[4]), .Carry_out(adder_3_carry_out), .Output(out_4[5]));
  Adder adder_4 (
    .INVA(Opcode[1]), .A(A[4]), .ENA(Opcode[3]), .B(B[4]), .ENB(Opcode[2]), .Carry_in(adder_3_carry_out),
    .F0(Opcode[5]), .F1(Opcode[4]), .Carry_out(adder_4_carry_out), .Output(out_4[4]));
  Adder adder_5 (
    .INVA(Opcode[1]), .A(A[3]), .ENA(Opcode[3]), .B(B[3]), .ENB(Opcode[2]), .Carry_in(adder_4_carry_out),
    .F0(Opcode[5]), .F1(Opcode[4]), .Carry_out(adder_5_carry_out), .Output(out_4[3]));
  Adder adder_6 (
    .INVA(Opcode[1]), .A(A[2]), .ENA(Opcode[3]), .B(B[2]), .ENB(Opcode[2]), .Carry_in(adder_5_carry_out),
    .F0(Opcode[5]), .F1(Opcode[4]), .Carry_out(adder_6_carry_out), .Output(out_4[2]));
  Adder adder_7 (
    .INVA(Opcode[1]), .A(A[1]), .ENA(Opcode[3]), .B(B[1]), .ENB(Opcode[2]), .Carry_in(adder_6_carry_out),
    .F0(Opcode[5]), .F1(Opcode[4]), .Carry_out(adder_7_carry_out), .Output(out_4[1]));
  Adder adder_8 (
    .INVA(Opcode[1]), .A(A[0]), .ENA(Opcode[3]), .B(B[0]), .ENB(Opcode[2]), .Carry_in(adder_7_carry_out),
    .F0(Opcode[5]), .F1(Opcode[4]), .Output(out_4[0]));  // open: Carry_out

  // Notes on the sheet:
  //   Lab 8
  //   Jacob, Christoss, Graham
endmodule

module Adder (
  input  INVA,
  input  A,
  input  ENA,
  input  B,
  input  ENB,
  input  Carry_in,
  input  F0,
  input  F1,
  output Output,
  output Carry_out
);

  wire A_out, and_1_out, and_2_out, and_3_out, and_4_out, and_5_out, and_6_out, B_out, C_out, D_out,
       hold_1_bit_1_sum, not_1_out, not_2_out, not_3_out, not_4_out, not_5_out, or_1_out, xor_1_out;

  not not_1 (not_1_out, F0);
  xor xor_1 (xor_1_out, INVA, and_1_out);
  and and_1 (and_1_out, A, ENA);
  and and_2 (and_2_out, B, ENB);
  not not_2 (not_2_out, F1);
  not not_3 (not_3_out, F0);
  not not_4 (not_4_out, F1);
  and u_A (A_out, not_1_out, not_2_out);
  and u_B (B_out, not_3_out, F1);
  and C (C_out, F0, not_4_out);
  and D (D_out, F0, F1);
  and and_3 (and_3_out, xor_1_out, and_2_out);
  or or_1 (or_1_out, xor_1_out, and_2_out);
  not not_5 (not_5_out, and_2_out);
  and and_4 (and_4_out, and_3_out, A_out);
  and and_5 (and_5_out, or_1_out, B_out);
  and and_6 (and_6_out, not_5_out, C_out);
  hold_1_bit hold_1_bit_1 (
    .Carry_in(Carry_in), .A(and_2_out), .B(xor_1_out), .in_4(D_out), .Carry_out(Carry_out),
    .Sum(hold_1_bit_1_sum));
  or or_2 (Output, and_4_out, and_5_out, and_6_out, hold_1_bit_1_sum);

  // Notes on the sheet:
  //   AB
  //   A+B
  //   Not B
  //   Sum
endmodule

module ALU_Packaged (
);

  main main_1 ();  // open: A, B, Opcode, out_4
endmodule

module hold_1_bit (
  input  Carry_in,
  input  A,
  input  B,
  input  in_4,
  output Sum,
  output Carry_out
);

  wire and_1_out, and_2_out, xor_1_out, xor_2_out;

  and and_1 (and_1_out, in_4, B, A);
  xor xor_1 (xor_1_out, A, B);
  or or_1 (Carry_out, and_1_out, and_2_out);
  and and_2 (and_2_out, in_4, Carry_in, xor_1_out);
  xor xor_2 (xor_2_out, Carry_in, xor_1_out);
  and and_3 (Sum, xor_2_out, in_4);
endmodule
