// Logisim project Controller.circ as structural Verilog: 1 circuit, main circuit Control Store
module Control_Store (
  input  [7:0] Instruction,
  input  [7:0] Immediate,
  input  in_3,
  output [7:0] ImmOut,
  output Imm,
  output [5:0] _6_bit_ALU_Opcode,
  output [1:0] Source,
  output [1:0] Destination
);

  wire and_1_out, and_2_out, and_3_out, and_4_out, and_5_out, and_6_out, and_7_out, and_8_out, and_9_out,
       and_10_out, and_11_out, and_12_out, and_13_out, and_14_out, and_15_out, not_1_out, not_2_out,
       not_3_out, not_4_out, not_5_out;

  not not_1 (not_1_out, Instruction[7]);
  not not_2 (not_2_out, Instruction[6]);
  not not_3 (not_3_out, Instruction[5]);
  not not_4 (not_4_out, Instruction[4]);
  and and_1 (and_1_out, not_1_out, not_2_out);
  and and_2 (and_2_out, not_2_out, Instruction[4]);
  or or_1 (_6_bit_ALU_Opcode[5], and_1_out, and_2_out, and_3_out);
  and and_3 (and_3_out, Instruction[5], not_4_out);
  or or_2 (_6_bit_ALU_Opcode[4], not_2_out, Instruction[5], Instruction[4]);
  Multiplexer #(.width(2)) multiplexer_1 (
    .in0(Instruction[3:2]), .in1(Instruction[1:0]), .out(Destination), .sel(not_5_out), .en(in_3));
  or or_3 (_6_bit_ALU_Opcode[3], Instruction[7], Instruction[6], Instruction[5], not_4_out);
  and and_4 (and_4_out, not_1_out, not_3_out, Instruction[4]);
  and and_5 (and_5_out, Instruction[6], not_3_out);
  or or_4 (_6_bit_ALU_Opcode[2], and_4_out, and_5_out, and_6_out);
  not not_5 (not_5_out, and_15_out);
  and and_6 (and_6_out, not_2_out, Instruction[5]);
  and and_7 (and_7_out, not_2_out, Instruction[4]);
  or or_5 (_6_bit_ALU_Opcode[1], and_7_out, and_8_out);
  and and_8 (and_8_out, Instruction[7], not_2_out, not_3_out);
  and and_9 (and_9_out, not_1_out, not_2_out, Instruction[5], not_4_out);
  and and_10 (and_10_out, not_2_out, Instruction[5], Instruction[4]);
  or or_6 (_6_bit_ALU_Opcode[0], and_9_out, and_10_out, and_11_out);
  and and_11 (and_11_out, Instruction[7], not_2_out, Instruction[4]);
  and and_12 (and_12_out, Instruction[7], Instruction[6], not_3_out);
  and and_13 (and_13_out, Instruction[7], not_2_out, Instruction[5]);
  or or_7 (Imm, and_12_out, and_13_out, and_14_out);
  and and_14 (and_14_out, Instruction[7], Instruction[5], Instruction[4]);
  and and_15 (and_15_out, not_2_out, not_3_out);

  assign ImmOut = Immediate;
  assign Source = Instruction[3:2];

  // Notes on the sheet:
  //   A
  //   B
  //   C
  //   D
  //   4 Bit Opcode Instruction
  //   Source and Destination bits
  //   F0
  //   F1
  //   ENA
  //   ENB
  //   if unary operation is on then the source is the destination 
  //   INVA
  //   INC
  //   Unary
endmodule
