// Logisim project Jk flip flop.circ as structural Verilog: 1 circuit, main circuit main
module main (
  input  J,
  input  in_2,
  input  in_3,
  input  in_4,
  input  in_5,
  input  Clear,
  output out_7,
  output not_Q
);

  J_K_Flip_Flop j_k_ff_1 (.J(J), .clk(in_2), .K(in_3), .Q(out_7), .Qn(not_Q), .preset(in_4), .en(in_5), .reset(Clear));

  // Notes on the sheet:
  //   Clock
  //   K
  //   Preset
  //   Enable
  //   Q
endmodule
