// Logisim project ShoresExample.circ as structural Verilog: 2 circuits, main circuit main
module main (
  input  Clear,
  input  Enable,
  input  Clock,
  input  Clear_2,
  input  Chip_Select,
  input  Clock_2,
  input  Load_Data,
  output [7:0] Current_Addr,
  output [7:0] _8_bit_inst,
  output [7:0] _8_bit_imm_value
);

  wire [15:0] ram_1_data;

  PC_IR pc_ir_1 (
    .Clear(Clear), .enable(Enable), .Clock(Clock), .instruction(_8_bit_inst), .addr_out(Current_Addr),
    .data_in(ram_1_data), .immediate_value(_8_bit_imm_value));
  RAM #(.dataWidth(16)) ram_1 (
    .addr(Current_Addr), .data(ram_1_data), .sel(Chip_Select), .clk(Clock_2), .ld(Load_Data), .clr(Clear_2));

  // Notes on the sheet:
  //   Load RAM with program
  //   Enable the PC_IR chip
  //   Each time you clock 0-->1-->0
  //   Next instruction is loaded 
  //   Note: data can flow either direction - in or out of RAM
  //   We only need data flowing out of RAM
  //   Turn on Chip Select and Load Data
  //   Do Not Clock, it's used to move data into RAM
endmodule

module PC_IR (
  input  Clear,
  input  enable,
  input  Clock,
  input  [15:0] data_in,
  output [7:0] addr_out,
  output [7:0] instruction,
  output [7:0] immediate_value
);

  wire [7:0] adder_1_out;

  Register PC (.D(adder_1_out), .en(enable), .Q(addr_out), .clk(Clock), .clr(Clear));
  Register #(.width(16)) IR (.D(data_in), .en(enable), .Q({instruction, immediate_value}), .clk(Clock), .clr(Clear));
  Adder adder_1 (.a(8'h1), .b(addr_out), .out(adder_1_out), .cin(1'b0));  // open: cout
endmodule
